# Fritzing sketch mugCircuit (saved by Fritzing 0.9.2b)
breadboards: 1

parts:
  U1 = ATTINY13 [package=dip]
  VCC1 = Battery [part_number="AAA Batery"]
  S1 = Pushbutton [package="[THT]"]
  LED1 = LED - 3mm [color="Green (555nm)" package="3 mm [THT]"]
  Q1 = NPN-Transistor [part_number=BC548 package="TO92 [THT]"]
  R1 = Resistor [tolerance=±5% resistance=1k package="0603 [SMD]"]
  D1 = Rectifier Diode [part_number=1N4001 package="300 mil [THT]"]
  M1 = DC Motor [part_number="DC Motor"]
  C1 = Electrolytic Capacitor [capacitance=10µF package="1010 [SMD, electrolytic]"]
  C2 = Capacitor [part_number=100nF package=cap-pth-small2]
  U2 = AVR 10-pin ICSP Header [part_number="ISP Header 10-pin" package=avr_icsp]

nets:
  N1: U1.PB5(NRES), U2.5
  N2: U1.PB3(ADC3), R1.Pin_1
  N3: U1.GND, VCC1.-, S1.Pin_3, S1.Pin_4, LED1.cathode, Q1.E, C1.-, U2.10
  N4: U1.PB0(MOSI), U2.1
  N5: U1.PB1(MISO), S1.Pin_1, S1.Pin_2, U2.9
  N6: U1.PB2(SCK_ADC1), LED1.anode, U2.7
  N7: U1.VCC, VCC1.+, D1.cathode, M1.pin_1, C1.+, C2.1, U2.2
  N8: Q1.B, R1.Pin_0
  N9: Q1.C, D1.anode, M1.pin_2, C2.2
